// Logisim project w2_1bit_full_adder.circ as structural Verilog: 1 circuit, main circuit main
module main (
  input  Cin,
  input  A,
  input  B,
  output Sum,
  output Carry
);

  wire and_1_out, and_2_out, and_3_out, xor_1_out;

  xor xor_1 (xor_1_out, Cin, A);
  and and_1 (and_1_out, Cin, A);
  and and_2 (and_2_out, A, B);
  and and_3 (and_3_out, Cin, B);
  xor xor_2 (Sum, xor_1_out, B);
  or or_1 (Carry, and_1_out, and_2_out, and_3_out);
endmodule
