// Logisim project w3_32kb_RAM.circ as structural Verilog: 12 circuits, main circuit main
module main (
  input  load,
  input  [5:0] address,
  input  [15:0] in,
  output [15:0] out
);

  wire CLK_out, load_plexer_1_load0, load_plexer_1_load1, load_plexer_1_load2, load_plexer_1_load3,
       load_plexer_1_load4, load_plexer_1_load5, load_plexer_1_load6, load_plexer_1_load7;
  wire [15:0] address_demulti_1__0, address_demulti_1__1, address_demulti_1__2, address_demulti_1__3,
       address_demulti_1__4, address_demulti_1__5, address_demulti_1__6, address_demulti_1__7, n8word_1_out,
       n8word_2_out, n8word_3_out, n8word_4_out, n8word_5_out, n8word_6_out, n8word_7_out, n8word_8_out;

  address_demulti address_demulti_1 (
    .in(in), .address(address[5:3]), ._0(address_demulti_1__0), ._1(address_demulti_1__1),
    ._2(address_demulti_1__2), ._3(address_demulti_1__3), ._4(address_demulti_1__4),
    ._5(address_demulti_1__5), ._6(address_demulti_1__6), ._7(address_demulti_1__7));
  load_plexer load_plexer_1 (
    .address(address[5:3]), .load(load), .load0(load_plexer_1_load0), .load1(load_plexer_1_load1),
    .load2(load_plexer_1_load2), .load3(load_plexer_1_load3), .load4(load_plexer_1_load4),
    .load5(load_plexer_1_load5), .load6(load_plexer_1_load6), .load7(load_plexer_1_load7));
  _8word u_8word_1 (
    .in(address_demulti_1__0), .out(n8word_1_out), .address(address[2:0]), .load(load_plexer_1_load0),
    .CLK(CLK_out));
  _8word u_8word_2 (
    .in(address_demulti_1__2), .out(n8word_2_out), .address(address[2:0]), .load(load_plexer_1_load2),
    .CLK(CLK_out));
  _8word u_8word_3 (
    .in(address_demulti_1__4), .out(n8word_3_out), .address(address[2:0]), .load(load_plexer_1_load4),
    .CLK(CLK_out));
  _8word u_8word_4 (
    .in(address_demulti_1__6), .out(n8word_4_out), .address(address[2:0]), .load(load_plexer_1_load6),
    .CLK(CLK_out));
  Clock CLK (.out(CLK_out));
  _8word u_8word_5 (
    .in(address_demulti_1__1), .out(n8word_5_out), .address(address[2:0]), .load(load_plexer_1_load1),
    .CLK(CLK_out));
  _8word u_8word_6 (
    .in(address_demulti_1__3), .out(n8word_6_out), .address(address[2:0]), .load(load_plexer_1_load3),
    .CLK(CLK_out));
  _8word u_8word_7 (
    .in(address_demulti_1__5), .out(n8word_7_out), .address(address[2:0]), .load(load_plexer_1_load5),
    .CLK(CLK_out));
  _8word u_8word_8 (
    .in(address_demulti_1__7), .out(n8word_8_out), .address(address[2:0]), .load(load_plexer_1_load7),
    .CLK(CLK_out));
  address_plexer address_plexer_1 (
    ._0(n8word_1_out), ._1(n8word_5_out), ._2(n8word_2_out), ._3(n8word_6_out), ._4(n8word_3_out),
    ._6(n8word_4_out), ._5(n8word_7_out), ._7(n8word_8_out), .out_10(out), .address(address[5:3]));
endmodule

module RS (
  input  R,
  input  S,
  output Q,
  output nQ
);

  nand nand_1 (Q, R, nQ);
  nand nand_2 (nQ, Q, S);
endmodule

module D (
  input  en,
  input  D,
  output Q,
  output nQ
);

  wire nand_1_out, nand_2_out, not_1_out;

  not not_1 (not_1_out, D);
  nand nand_1 (nand_1_out, en, not_1_out);
  nand nand_2 (nand_2_out, en, D);
  RS rs_1 (.R(nand_1_out), .Q(Q), .nQ(nQ), .S(nand_2_out));
endmodule

module multiplexer (
  input  Sel,
  input  A,
  input  B,
  output O
);

  wire and_1_out, and_2_out, not_1_out;

  not not_1 (not_1_out, Sel);
  and and_1 (and_1_out, not_1_out, A);
  and and_2 (and_2_out, Sel, B);
  or or_1 (O, and_1_out, and_2_out);
endmodule

module DFF (
  input  CLK,
  input  D,
  output Q,
  output nQ
);

  wire d_1_q, not_1_out;

  not not_1 (not_1_out, CLK);
  D d_1 (.en(not_1_out), .Q(d_1_q), .D(D));  // open: nQ
  D d_2 (.en(CLK), .Q(Q), .nQ(nQ), .D(d_1_q));
endmodule

module _1bit_register (
  input  load,
  input  CLK,
  input  in,
  output O
);

  wire multiplexer_1_o;

  multiplexer multiplexer_1 (.A(O), .B(in), .Sel(load), .O(multiplexer_1_o));
  DFF dff_1 (.CLK(CLK), .D(multiplexer_1_o), .Q(O));  // open: nQ
endmodule

module _16bit_register (
  input  load,
  input  [15:0] in,
  input  CLK,
  output [15:0] out
);

  _1bit_register _0 (.in(in[0]), .O(out[0]), .load(load), .CLK(CLK));
  _1bit_register _2 (.in(in[2]), .O(out[2]), .load(load), .CLK(CLK));
  _1bit_register _4 (.in(in[4]), .O(out[4]), .load(load), .CLK(CLK));
  _1bit_register _6 (.in(in[6]), .O(out[6]), .load(load), .CLK(CLK));
  _1bit_register _8 (.in(in[8]), .O(out[8]), .load(load), .CLK(CLK));
  _1bit_register _10 (.in(in[10]), .O(out[10]), .load(load), .CLK(CLK));
  _1bit_register _12 (.in(in[12]), .O(out[12]), .load(load), .CLK(CLK));
  _1bit_register _14 (.in(in[14]), .O(out[14]), .load(load), .CLK(CLK));
  _1bit_register _1 (.in(in[1]), .O(out[1]), .load(load), .CLK(CLK));
  _1bit_register _3 (.in(in[3]), .O(out[3]), .load(load), .CLK(CLK));
  _1bit_register _5 (.in(in[5]), .O(out[5]), .load(load), .CLK(CLK));
  _1bit_register _7 (.in(in[7]), .O(out[7]), .load(load), .CLK(CLK));
  _1bit_register _9 (.in(in[9]), .O(out[9]), .load(load), .CLK(CLK));
  _1bit_register _11 (.in(in[11]), .O(out[11]), .load(load), .CLK(CLK));
  _1bit_register _13 (.in(in[13]), .O(out[13]), .load(load), .CLK(CLK));
  _1bit_register _15 (.in(in[15]), .O(out[15]), .load(load), .CLK(CLK));
endmodule

module address_plexer (
  input  [15:0] _0,
  input  [2:0] address,
  input  [15:0] _1,
  input  [15:0] _2,
  input  [15:0] _3,
  input  [15:0] _4,
  input  [15:0] _6,
  input  [15:0] _5,
  input  [15:0] _7,
  output [15:0] out_10
);

  wire not_1_out, not_2_out, not_3_out;
  wire [15:0] and_1_out, and_2_out, and_3_out, and_4_out, and_5_out, and_6_out, and_7_out, and_8_out;
  wire [15:15] _000_out, _001_out, _010_out, _011_out, _100_out, _101_out, _110_out, _111_out;

  not not_1 (not_1_out, address[1]);
  not not_2 (not_2_out, address[2]);
  not not_3 (not_3_out, address[0]);
  and _000 (_000_out[15], not_3_out, not_1_out, not_2_out);
  and _001 (_001_out[15], not_2_out, not_1_out, address[0]);
  and _010 (_010_out[15], not_2_out, address[1], not_3_out);
  and _011 (_011_out[15], not_2_out, address[1], address[0]);
  and _100 (_100_out[15], address[2], not_1_out, not_3_out);
  and _101 (_101_out[15], address[2], not_1_out, address[0]);
  and _110 (_110_out[15], address[2], address[1], not_3_out);
  and _111 (_111_out[15], address[2], address[1], address[0]);
  assign and_1_out = _0 & {16{_000_out[15]}};  // AND_Gate and_1, 16 bits wide
  assign and_2_out = _4 & {16{_100_out[15]}};  // AND_Gate and_2, 16 bits wide
  assign and_3_out = _1 & {16{_001_out[15]}};  // AND_Gate and_3, 16 bits wide
  assign and_4_out = _5 & {16{_101_out[15]}};  // AND_Gate and_4, 16 bits wide
  assign and_5_out = _2 & {16{_010_out[15]}};  // AND_Gate and_5, 16 bits wide
  assign and_6_out = _3 & {16{_011_out[15]}};  // AND_Gate and_6, 16 bits wide
  assign and_7_out = _6 & {16{_110_out[15]}};  // AND_Gate and_7, 16 bits wide
  assign and_8_out = _7 & {16{_111_out[15]}};  // AND_Gate and_8, 16 bits wide
  assign out_10 = and_1_out | and_3_out | and_5_out | and_6_out | and_7_out | and_8_out | and_4_out | and_2_out;  // OR_Gate or_1, 16 bits wide
endmodule

module address_demulti (
  input  [15:0] in,
  input  [2:0] address,
  output [15:0] _0,
  output [15:0] _1,
  output [15:0] _2,
  output [15:0] _3,
  output [15:0] _4,
  output [15:0] _5,
  output [15:0] _6,
  output [15:0] _7
);

  wire not_1_out, not_2_out, not_3_out;
  wire [15:15] _000_out, _001_out, _010_out, _011_out, _100_out, _101_out, _110_out, _111_out;

  not not_1 (not_1_out, address[1]);
  not not_2 (not_2_out, address[2]);
  not not_3 (not_3_out, address[0]);
  and _000 (_000_out[15], not_3_out, not_1_out, not_2_out);
  and _001 (_001_out[15], not_2_out, not_1_out, address[0]);
  and _010 (_010_out[15], not_2_out, address[1], not_3_out);
  and _011 (_011_out[15], not_2_out, address[1], address[0]);
  and _100 (_100_out[15], address[2], not_1_out, not_3_out);
  and _101 (_101_out[15], address[2], not_1_out, address[0]);
  and _110 (_110_out[15], address[2], address[1], not_3_out);
  and _111 (_111_out[15], address[2], address[1], address[0]);
  assign _0 = in & {16{_000_out[15]}};  // AND_Gate and_1, 16 bits wide
  assign _1 = in & {16{_001_out[15]}};  // AND_Gate and_2, 16 bits wide
  assign _2 = in & {16{_010_out[15]}};  // AND_Gate and_3, 16 bits wide
  assign _3 = in & {16{_011_out[15]}};  // AND_Gate and_4, 16 bits wide
  assign _4 = in & {16{_100_out[15]}};  // AND_Gate and_5, 16 bits wide
  assign _5 = in & {16{_101_out[15]}};  // AND_Gate and_6, 16 bits wide
  assign _6 = in & {16{_110_out[15]}};  // AND_Gate and_7, 16 bits wide
  assign _7 = in & {16{_111_out[15]}};  // AND_Gate and_8, 16 bits wide
endmodule

module load_plexer (
  input  [2:0] address,
  input  load,
  output load0,
  output load1,
  output load2,
  output load3,
  output load4,
  output load5,
  output load6,
  output load7
);

  wire not_1_out, not_2_out, not_3_out;

  not not_1 (not_1_out, address[1]);
  not not_2 (not_2_out, address[2]);
  not not_3 (not_3_out, address[0]);
  and _000 (load0, not_3_out, not_1_out, not_2_out, load);
  and _001 (load1, address[0], not_1_out, not_2_out, load);
  and _010 (load2, not_3_out, address[1], not_2_out, load);
  and _011 (load3, address[0], address[1], not_2_out, load);
  and _100 (load4, not_3_out, not_1_out, address[2], load);
  and _101 (load5, address[0], not_1_out, address[2], load);
  and _110 (load6, not_3_out, address[1], address[2], load);
  and _111 (load7, address[0], address[1], address[2], load);
endmodule

module _8word (
  input  [2:0] address,
  input  load,
  input  [15:0] in,
  input  CLK,
  output [15:0] out
);

  wire load_plexer_1_load0, load_plexer_1_load1, load_plexer_1_load2, load_plexer_1_load3,
       load_plexer_1_load4, load_plexer_1_load5, load_plexer_1_load6, load_plexer_1_load7;
  wire [15:0] address_demulti_1__0, address_demulti_1__1, address_demulti_1__2, address_demulti_1__3,
       address_demulti_1__4, address_demulti_1__5, address_demulti_1__6, address_demulti_1__7,
       n16bit_register_1_out, n16bit_register_2_out, n16bit_register_3_out, n16bit_register_4_out,
       n16bit_register_5_out, n16bit_register_6_out, n16bit_register_7_out, n16bit_register_8_out;

  address_demulti address_demulti_1 (
    .in(in), .address(address), ._0(address_demulti_1__0), ._1(address_demulti_1__1),
    ._2(address_demulti_1__2), ._3(address_demulti_1__3), ._4(address_demulti_1__4),
    ._5(address_demulti_1__5), ._6(address_demulti_1__6), ._7(address_demulti_1__7));
  _16bit_register u_16bit_register_1 (
    .in(address_demulti_1__0), .out(n16bit_register_1_out), .load(load_plexer_1_load0), .CLK(CLK));
  _16bit_register u_16bit_register_2 (
    .in(address_demulti_1__2), .out(n16bit_register_2_out), .load(load_plexer_1_load2), .CLK(CLK));
  _16bit_register u_16bit_register_3 (
    .in(address_demulti_1__4), .out(n16bit_register_3_out), .load(load_plexer_1_load4), .CLK(CLK));
  _16bit_register u_16bit_register_4 (
    .in(address_demulti_1__6), .out(n16bit_register_4_out), .load(load_plexer_1_load6), .CLK(CLK));
  load_plexer load_plexer_1 (
    .address(address), .load(load), .load0(load_plexer_1_load0), .load1(load_plexer_1_load1),
    .load2(load_plexer_1_load2), .load3(load_plexer_1_load3), .load4(load_plexer_1_load4),
    .load5(load_plexer_1_load5), .load6(load_plexer_1_load6), .load7(load_plexer_1_load7));
  _16bit_register u_16bit_register_5 (
    .in(address_demulti_1__1), .out(n16bit_register_5_out), .load(load_plexer_1_load1), .CLK(CLK));
  _16bit_register u_16bit_register_6 (
    .in(address_demulti_1__3), .out(n16bit_register_6_out), .load(load_plexer_1_load3), .CLK(CLK));
  _16bit_register u_16bit_register_7 (
    .in(address_demulti_1__5), .out(n16bit_register_7_out), .load(load_plexer_1_load5), .CLK(CLK));
  _16bit_register u_16bit_register_8 (
    .in(address_demulti_1__7), .out(n16bit_register_8_out), .load(load_plexer_1_load7), .CLK(CLK));
  address_plexer address_plexer_1 (
    ._0(n16bit_register_1_out), ._1(n16bit_register_5_out), ._2(n16bit_register_2_out),
    ._3(n16bit_register_6_out), ._4(n16bit_register_3_out), ._6(n16bit_register_4_out),
    ._5(n16bit_register_7_out), ._7(n16bit_register_8_out), .out_10(out), .address(address));
endmodule

module _64word (
  input  load,
  input  [5:0] address,
  input  [15:0] in,
  output [15:0] out
);

  wire CLK_out, load_plexer_1_load0, load_plexer_1_load1, load_plexer_1_load2, load_plexer_1_load3,
       load_plexer_1_load4, load_plexer_1_load5, load_plexer_1_load6, load_plexer_1_load7;
  wire [15:0] address_demulti_1__0, address_demulti_1__1, address_demulti_1__2, address_demulti_1__3,
       address_demulti_1__4, address_demulti_1__5, address_demulti_1__6, address_demulti_1__7, n8word_1_out,
       n8word_2_out, n8word_3_out, n8word_4_out, n8word_5_out, n8word_6_out, n8word_7_out, n8word_8_out;

  address_demulti address_demulti_1 (
    .in(in), .address(address[5:3]), ._0(address_demulti_1__0), ._1(address_demulti_1__1),
    ._2(address_demulti_1__2), ._3(address_demulti_1__3), ._4(address_demulti_1__4),
    ._5(address_demulti_1__5), ._6(address_demulti_1__6), ._7(address_demulti_1__7));
  load_plexer load_plexer_1 (
    .address(address[5:3]), .load(load), .load0(load_plexer_1_load0), .load1(load_plexer_1_load1),
    .load2(load_plexer_1_load2), .load3(load_plexer_1_load3), .load4(load_plexer_1_load4),
    .load5(load_plexer_1_load5), .load6(load_plexer_1_load6), .load7(load_plexer_1_load7));
  _8word u_8word_1 (
    .in(address_demulti_1__0), .out(n8word_1_out), .address(address[2:0]), .load(load_plexer_1_load0),
    .CLK(CLK_out));
  _8word u_8word_2 (
    .in(address_demulti_1__2), .out(n8word_2_out), .address(address[2:0]), .load(load_plexer_1_load2),
    .CLK(CLK_out));
  _8word u_8word_3 (
    .in(address_demulti_1__4), .out(n8word_3_out), .address(address[2:0]), .load(load_plexer_1_load4),
    .CLK(CLK_out));
  _8word u_8word_4 (
    .in(address_demulti_1__6), .out(n8word_4_out), .address(address[2:0]), .load(load_plexer_1_load6),
    .CLK(CLK_out));
  Clock CLK (.out(CLK_out));
  _8word u_8word_5 (
    .in(address_demulti_1__1), .out(n8word_5_out), .address(address[2:0]), .load(load_plexer_1_load1),
    .CLK(CLK_out));
  _8word u_8word_6 (
    .in(address_demulti_1__3), .out(n8word_6_out), .address(address[2:0]), .load(load_plexer_1_load3),
    .CLK(CLK_out));
  _8word u_8word_7 (
    .in(address_demulti_1__5), .out(n8word_7_out), .address(address[2:0]), .load(load_plexer_1_load5),
    .CLK(CLK_out));
  _8word u_8word_8 (
    .in(address_demulti_1__7), .out(n8word_8_out), .address(address[2:0]), .load(load_plexer_1_load7),
    .CLK(CLK_out));
  address_plexer address_plexer_1 (
    ._0(n8word_1_out), ._1(n8word_5_out), ._2(n8word_2_out), ._3(n8word_6_out), ._4(n8word_3_out),
    ._6(n8word_4_out), ._5(n8word_7_out), ._7(n8word_8_out), .out_10(out), .address(address[5:3]));
endmodule
