// Logisim project w3_flipflops.circ as structural Verilog
module RS (
  input  R,
  input  S,
  output Q,
  output nQ
);

  nand nand_1 (Q, R, nQ);
  nand nand_2 (nQ, Q, S);
endmodule

module D (
  input  en,
  input  D,
  output Q,
  output nQ
);

  wire nand_1_out, nand_2_out, not_1_out;

  not not_1 (not_1_out, D);
  nand nand_1 (nand_1_out, en, not_1_out);
  nand nand_2 (nand_2_out, en, D);
  RS rs_1 (.R(nand_1_out), .Q(Q), .nQ(nQ), .S(nand_2_out));
endmodule

module DFF (
  input  CLK,
  input  D,
  input  CLK_2,
  input  D_2,
  output Q,
  output nQ,
  output Q_2,
  output nQ_2
);

  wire _1_out, _3_out, _4_out, _5_out, _6_out, _7_out, _8_out, _9_out, d_1_q, not_1_out, not_2_out;

  not not_1 (not_1_out, CLK);
  D d_1 (.en(not_1_out), .Q(d_1_q), .D(D));  // open: nQ
  not not_2 (not_2_out, CLK_2);
  not _1 (_1_out, D_2);
  D u_d_2 (.en(CLK), .Q(Q), .nQ(nQ), .D(d_1_q));
  nand _3 (_3_out, not_2_out, _1_out);
  nand _4 (_4_out, not_2_out, D_2);
  nand _5 (_5_out, _3_out, _6_out);
  nand _6 (_6_out, _5_out, _4_out);
  not _7 (_7_out, _5_out);
  nand _8 (_8_out, CLK_2, _7_out);
  nand _9 (_9_out, CLK_2, _5_out);
  nand _10 (Q_2, _8_out, nQ_2);
  nand _11 (nQ_2, Q_2, _9_out);
endmodule

module TFF (
  output out_1
);

  wire clock_1_out, not_1_out;

  Clock clock_1 (.out(clock_1_out));
  not not_1 (not_1_out, out_1);
  D_Flip_Flop d_ff_1 (.clk(clock_1_out), .D(not_1_out), .Q(out_1));  // open: Qn, preset, en, reset
endmodule

module JKFF (
  input  J,
  input  K,
  output out_3,
  output out_4
);

  wire and_1_out, and_2_out, clock_1_out, not_1_out, or_1_out;

  not not_1 (not_1_out, K);
  and and_1 (and_1_out, J, out_4);
  or or_1 (or_1_out, and_1_out, and_2_out);
  and and_2 (and_2_out, not_1_out, out_3);
  Clock clock_1 (.out(clock_1_out));
  D_Flip_Flop d_ff_1 (.clk(clock_1_out), .D(or_1_out), .Q(out_3), .Qn(out_4));  // open: preset, en, reset
endmodule
