// Logisim project w4_traffic.circ as structural Verilog: 5 circuits, main circuit main
module main (
  input  button
);

  wire a2r_done, demultiplexer_1_out0, demultiplexer_1_out2, demultiplexer_1_out4, demultiplexer_1_out8,
       f2g_done, one_shot_1_out, one_shot_2_out, one_shot_3_out, one_shot_4_out, or_1_out, or_2_out, r2f_done;
  wire [3:0] brain_1_next_status;

  timer a2r (.\time (16'h400), .go(button), .done(a2r_done));
  timer r2f (.\time (16'h1e00), .go(a2r_done), .done(r2f_done));
  timer f2g (.\time (16'ha00), .go(r2f_done), .done(f2g_done));
  one_shot one_shot_1 (.in(f2g_done), .out(one_shot_1_out));
  one_shot one_shot_2 (.in(r2f_done), .out(one_shot_2_out));
  one_shot one_shot_3 (.in(a2r_done), .out(one_shot_3_out));
  one_shot one_shot_4 (.in(button), .out(one_shot_4_out));
  Demultiplexer #(.select(4)) demultiplexer_1 (
    .out0(demultiplexer_1_out0), .out2(demultiplexer_1_out2), .out4(demultiplexer_1_out4),
    .out8(demultiplexer_1_out8), .in(1'b1), .sel(brain_1_next_status));  // open: out1, out3, out5, out6, out7, out9, out10, out11, out12, out13, out14, out15, en
  or or_1 (or_1_out, one_shot_1_out, one_shot_2_out, one_shot_3_out, one_shot_4_out);
  brain brain_1 (.next_status(brain_1_next_status), .change(or_1_out));
  LED red (.in(demultiplexer_1_out2));
  LED amber (.in(demultiplexer_1_out4));
  or or_2 (or_2_out, demultiplexer_1_out0, demultiplexer_1_out8);
  LED green (.in(or_2_out));
endmodule

module one_shot (
  input  in,
  output out
);

  wire and_1_out, CLK_out, not_1_out, register_1_q;

  not not_1 (not_1_out, register_1_q);
  and and_1 (and_1_out, not_1_out, in);
  Clock CLK (.out(CLK_out));
  Register #(.width(1)) register_1 (.D(in), .en(1'b1), .Q(register_1_q), .clk(CLK_out));  // open: clr
  Register #(.width(1)) register_2 (.D(and_1_out), .en(1'b1), .Q(out), .clk(CLK_out));  // open: clr
endmodule

module brain (
  input  change,
  output [3:0] next_status
);

  wire clock_1_out, one_shot_1_out;
  wire [3:0] multiplexer_1_out;

  one_shot one_shot_1 (.in(change), .out(one_shot_1_out));
  Multiplexer #(.width(4)) multiplexer_1 (
    .in0(4'b1000), .in1({next_status[0], next_status[3:1]}), .out(multiplexer_1_out), .sel(one_shot_1_out));  // open: en
  Register #(.width(4)) register_1 (
    .D(multiplexer_1_out), .en(one_shot_1_out), .Q(next_status), .clk(clock_1_out));  // open: clr
  Clock clock_1 (.out(clock_1_out));
endmodule

module timer (
  input  [15:0] \time ,
  input  go,
  output done
);

  wire clock_1_out, clock_2_out, comparator_1_output, multiplexer_2_out, not_1_out, one_shot_1_out, or_1_out;
  wire [15:0] adder_1_out, multiplexer_1_out, register_1_q;

  Adder #(.width(16)) adder_1 (.a(16'h1), .b(register_1_q), .out(adder_1_out));  // open: cin, cout
  Multiplexer #(.width(16)) multiplexer_1 (
    .in0({16{1'b0}}), .in1(adder_1_out), .out(multiplexer_1_out), .sel(go));  // open: en
  Register #(.width(16)) register_1 (.D(multiplexer_1_out), .Q(register_1_q), .clk(clock_1_out));  // open: en, clr
  Clock clock_1 (.out(clock_1_out));
  comparator comparator_1 (.input1(\time ), .input2(register_1_q), .\output (comparator_1_output));
  not not_1 (not_1_out, go);
  Multiplexer multiplexer_2 (.in0(1'b0), .in1(1'b1), .out(multiplexer_2_out), .sel(comparator_1_output));  // open: en
  one_shot one_shot_1 (.in(not_1_out), .out(one_shot_1_out));
  or or_1 (or_1_out, comparator_1_output, one_shot_1_out);
  Register #(.width(1)) register_2 (.D(multiplexer_2_out), .en(or_1_out), .Q(done), .clk(clock_2_out));  // open: clr
  Clock clock_2 (.out(clock_2_out));
endmodule

module comparator (
  input  [15:0] input1,
  input  [15:0] input2,
  output \output 
);

  wire and_1_out, and_2_out, and_3_out, and_4_out;
  wire [15:0] not_1_out, xor_1_out;

  assign not_1_out = ~xor_1_out;  // NOT_Gate not_1, 16 bits wide
  assign xor_1_out = input1 ^ input2;  // XOR_Gate xor_1, 16 bits wide
  and and_1 (and_1_out, not_1_out[0], not_1_out[1], not_1_out[2], not_1_out[3]);
  and and_2 (and_2_out, not_1_out[4], not_1_out[5], not_1_out[6], not_1_out[7]);
  and and_3 (and_3_out, not_1_out[8], not_1_out[9], not_1_out[10], not_1_out[11]);
  and and_4 (and_4_out, not_1_out[12], not_1_out[13], not_1_out[14], not_1_out[15]);
  and and_5 (\output , and_1_out, and_2_out, and_3_out, and_4_out);
endmodule
